// Logisim project and.circ as structural Verilog: 1 circuit, main circuit main
module main (
  input  A,
  input  B,
  input  A_2,
  input  B_2,
  input  A_3,
  input  B_3
);

  wire and_1_out, nand_1_out, nand_2_out, pull_resistor_1_node, pull_resistor_2_node, transistor_2_out;

  and and_1 (and_1_out, A, B);
  nand nand_1 (nand_1_out, A_2, B_2);
  Pull_Resistor #(.pull(1)) pull_resistor_1 (.node(pull_resistor_1_node));
  Transistor #(.\type ("n")) transistor_1 (.in(transistor_2_out), .out(pull_resistor_1_node), .gate(A_3));
  Transistor #(.\type ("n")) transistor_2 (.in(1'b0), .out(transistor_2_out), .gate(B_3));
  LED OUT (.in(and_1_out));
  LED OUT_2 (.in(nand_2_out));
  nand nand_2 (nand_2_out, nand_1_out, nand_1_out);
  Pull_Resistor #(.pull(1)) pull_resistor_2 (.node(pull_resistor_2_node));
  Transistor #(.\type ("n")) transistor_3 (.in(1'b0), .out(pull_resistor_2_node), .gate(pull_resistor_1_node));
  LED OUT_3 (.in(pull_resistor_2_node));

  // Notes on the sheet:
  //   AND
endmodule
