// Logisim project dmux.circ as structural Verilog: 1 circuit, main circuit main
module main (
  input  IN,
  input  IN_2,
  input  SEL,
  input  IN_3,
  input  SEL_2,
  input  SEL_3,
  input  IN_4,
  input  SEL_4
);

  wire and_1_out, and_2_out, demultiplexer_1_out0, demultiplexer_1_out1, nand_1_out, nand_2_out, nand_3_out,
       nand_4_out, nand_5_out, not_1_out, pull_resistor_1_node, pull_resistor_2_node, pull_resistor_3_node,
       pull_resistor_4_node, pull_resistor_5_node, transistor_3_out, transistor_5_out;

  Demultiplexer #(.enable("false")) demultiplexer_1 (
    .out0(demultiplexer_1_out0), .out1(demultiplexer_1_out1), .in(IN), .sel(SEL));
  not not_1 (not_1_out, SEL_3);
  LED A (.in(demultiplexer_1_out0));
  LED B (.in(demultiplexer_1_out1));
  and and_1 (and_1_out, IN_3, not_1_out);
  and and_2 (and_2_out, SEL_3, IN_3);
  nand nand_1 (nand_1_out, SEL_4, SEL_4);
  LED A_2 (.in(and_1_out));
  LED B_2 (.in(and_2_out));
  nand nand_2 (nand_2_out, IN_4, nand_1_out);
  nand nand_3 (nand_3_out, SEL_4, IN_4);
  nand nand_4 (nand_4_out, nand_2_out, nand_2_out);
  nand nand_5 (nand_5_out, nand_3_out, nand_3_out);
  LED A_3 (.in(nand_4_out));
  LED B_3 (.in(nand_5_out));
  Pull_Resistor #(.pull(1)) pull_resistor_1 (.node(pull_resistor_1_node));
  Transistor #(.\type ("n")) transistor_1 (.in(1'b0), .out(pull_resistor_1_node), .gate(SEL_2));
  Pull_Resistor #(.pull(1)) pull_resistor_2 (.node(pull_resistor_2_node));
  Transistor #(.\type ("n")) transistor_2 (.in(transistor_3_out), .out(pull_resistor_2_node), .gate(IN_2));
  Transistor #(.\type ("n")) transistor_3 (.in(1'b0), .out(transistor_3_out), .gate(pull_resistor_1_node));
  Pull_Resistor #(.pull(1)) pull_resistor_3 (.node(pull_resistor_3_node));
  Transistor #(.\type ("n")) transistor_4 (.in(transistor_5_out), .out(pull_resistor_3_node), .gate(SEL_2));
  Transistor #(.\type ("n")) transistor_5 (.in(1'b0), .out(transistor_5_out), .gate(IN_2));
  Pull_Resistor #(.pull(1)) pull_resistor_4 (.node(pull_resistor_4_node));
  Transistor #(.\type ("n")) transistor_6 (.in(1'b0), .out(pull_resistor_4_node), .gate(pull_resistor_2_node));
  Pull_Resistor #(.pull(1)) pull_resistor_5 (.node(pull_resistor_5_node));
  Transistor #(.\type ("n")) transistor_7 (.in(1'b0), .out(pull_resistor_5_node), .gate(pull_resistor_3_node));
  LED A_4 (.in(pull_resistor_4_node));
  LED B_4 (.in(pull_resistor_5_node));

  // Notes on the sheet:
  //   DEMUX
endmodule
