// Logisim project dmux4way.circ as structural Verilog: 1 circuit, main circuit main
module main (
  input  IN,
  input  SEL_1,
  input  SEL_0,
  input  IN_2,
  input  SEL_1_2,
  input  SEL_0_2
);

  wire demultiplexer_1_out0, demultiplexer_1_out1, demultiplexer_2_out0, demultiplexer_2_out1,
       demultiplexer_3_out0, demultiplexer_3_out1, nand_1_out, nand_2_out, nand_3_out, nand_4_out,
       nand_5_out, nand_6_out, nand_7_out, nand_8_out, nand_9_out, nand_10_out, nand_11_out, nand_12_out,
       nand_13_out, nand_14_out, nand_15_out;

  Demultiplexer #(.enable("false")) demultiplexer_1 (
    .out0(demultiplexer_1_out0), .out1(demultiplexer_1_out1), .in(IN), .sel(SEL_1));
  nand nand_1 (nand_1_out, SEL_1_2, SEL_1_2);
  Demultiplexer #(.enable("false")) demultiplexer_2 (
    .out0(demultiplexer_2_out0), .out1(demultiplexer_2_out1), .in(demultiplexer_1_out0), .sel(SEL_0));
  Demultiplexer #(.enable("false")) demultiplexer_3 (
    .out0(demultiplexer_3_out0), .out1(demultiplexer_3_out1), .in(demultiplexer_1_out1), .sel(SEL_0));
  nand nand_2 (nand_2_out, IN_2, nand_1_out);
  nand nand_3 (nand_3_out, SEL_1_2, IN_2);
  LED A (.in(demultiplexer_2_out0));
  LED B (.in(demultiplexer_2_out1));
  LED C (.in(demultiplexer_3_out0));
  LED D (.in(demultiplexer_3_out1));
  nand nand_4 (nand_4_out, nand_2_out, nand_2_out);
  nand nand_5 (nand_5_out, nand_3_out, nand_3_out);
  nand nand_6 (nand_6_out, SEL_0_2, SEL_0_2);
  nand nand_7 (nand_7_out, SEL_0_2, SEL_0_2);
  nand nand_8 (nand_8_out, nand_4_out, nand_6_out);
  nand nand_9 (nand_9_out, SEL_0_2, nand_4_out);
  nand nand_10 (nand_10_out, nand_5_out, nand_7_out);
  nand nand_11 (nand_11_out, SEL_0_2, nand_5_out);
  nand nand_12 (nand_12_out, nand_8_out, nand_8_out);
  nand nand_13 (nand_13_out, nand_9_out, nand_9_out);
  nand nand_14 (nand_14_out, nand_10_out, nand_10_out);
  nand nand_15 (nand_15_out, nand_11_out, nand_11_out);
  LED A_2 (.in(nand_12_out));
  LED B_2 (.in(nand_13_out));
  LED C_2 (.in(nand_14_out));
  LED D_2 (.in(nand_15_out));

  // Notes on the sheet:
  //   DEMUX4WAY
endmodule
