// Logisim project mux.circ as structural Verilog: 1 circuit, main circuit main
module main (
  input  A,
  input  B,
  input  A_2,
  input  SEL,
  input  A_3,
  input  SEL_2,
  input  SEL_3,
  input  B_2,
  input  B_3,
  input  A_4,
  input  SEL_4,
  input  B_4
);

  wire multiplexer_1_out, nand_1_out, nand_2_out, nand_3_out, nand_4_out, nand_5_out, nand_6_out, nand_7_out,
       not_1_out, pull_resistor_1_node, pull_resistor_2_node, pull_resistor_3_node, pull_resistor_4_node,
       transistor_2_out, transistor_4_out, transistor_6_out, transistor_8_out;

  not not_1 (not_1_out, SEL_3);
  Multiplexer #(.enable("false")) multiplexer_1 (.in0(A), .in1(B), .out(multiplexer_1_out), .sel(SEL));
  LED OUT (.in(multiplexer_1_out));
  nand nand_1 (nand_1_out, SEL_3, B_2);
  nand nand_2 (nand_2_out, SEL_4, SEL_4);
  nand nand_3 (nand_3_out, A_3, not_1_out);
  nand nand_4 (nand_4_out, A_4, nand_2_out);
  nand nand_5 (nand_5_out, SEL_4, B_4);
  LED OUT_2 (.in(nand_6_out));
  nand nand_6 (nand_6_out, nand_3_out, nand_1_out);
  nand nand_7 (nand_7_out, nand_4_out, nand_5_out);
  LED OUT_3 (.in(nand_7_out));
  Pull_Resistor #(.pull(1)) pull_resistor_1 (.node(pull_resistor_1_node));
  Transistor #(.\type ("n")) transistor_1 (.in(transistor_2_out), .out(pull_resistor_1_node), .gate(SEL_2));
  Transistor #(.\type ("n")) transistor_2 (.in(1'b0), .out(transistor_2_out), .gate(SEL_2));
  Pull_Resistor #(.pull(1)) pull_resistor_2 (.node(pull_resistor_2_node));
  Transistor #(.\type ("n")) transistor_3 (.in(transistor_4_out), .out(pull_resistor_2_node), .gate(A_2));
  Transistor #(.\type ("n")) transistor_4 (.in(1'b0), .out(transistor_4_out), .gate(pull_resistor_1_node));
  Pull_Resistor #(.pull(1)) pull_resistor_3 (.node(pull_resistor_3_node));
  Transistor #(.\type ("n")) transistor_5 (.in(transistor_6_out), .out(pull_resistor_3_node), .gate(SEL_2));
  Transistor #(.\type ("n")) transistor_6 (.in(1'b0), .out(transistor_6_out), .gate(B_3));
  Pull_Resistor #(.pull(1)) pull_resistor_4 (.node(pull_resistor_4_node));
  Transistor #(.\type ("n")) transistor_7 (
    .in(transistor_8_out), .out(pull_resistor_4_node), .gate(pull_resistor_2_node));
  Transistor #(.\type ("n")) transistor_8 (.in(1'b0), .out(transistor_8_out), .gate(pull_resistor_3_node));
  LED OUT_4 (.in(pull_resistor_4_node));

  // Notes on the sheet:
  //   MUX
endmodule
