// Logisim project nand.circ as structural Verilog: 1 circuit, main circuit main
module main (
  input  A,
  input  B,
  input  A_2,
  input  B_2
);

  wire nand_1_out, pull_resistor_1_node, transistor_2_out;

  Pull_Resistor #(.pull(1)) pull_resistor_1 (.node(pull_resistor_1_node));
  Transistor #(.\type ("n")) transistor_1 (.in(transistor_2_out), .out(pull_resistor_1_node), .gate(A_2));
  Transistor #(.\type ("n")) transistor_2 (.in(1'b0), .out(transistor_2_out), .gate(B_2));
  nand nand_1 (nand_1_out, A, B);
  LED OUT (.in(nand_1_out));
  LED OUT_2 (.in(pull_resistor_1_node));

  // Notes on the sheet:
  //   NAND (Fundamental)
endmodule
