// Logisim project not.circ as structural Verilog: 1 circuit, main circuit main
module main (
  input  IN,
  input  IN_2,
  input  IN_3
);

  wire nand_1_out, not_1_out, pull_resistor_1_node;

  not not_1 (not_1_out, IN);
  Pull_Resistor #(.pull(1)) pull_resistor_1 (.node(pull_resistor_1_node));
  Transistor #(.\type ("n")) transistor_1 (.in(1'b0), .out(pull_resistor_1_node), .gate(IN_3));
  LED OUT (.in(not_1_out));
  nand nand_1 (nand_1_out, IN_2, IN_2);
  LED OUT_2 (.in(nand_1_out));
  LED OUT_3 (.in(pull_resistor_1_node));

  // Notes on the sheet:
  //   NOT
endmodule
