// Logisim project or.circ as structural Verilog: 1 circuit, main circuit main
module main (
  input  A,
  input  B,
  input  A_2,
  input  B_2,
  input  A_3,
  input  B_3,
  input  A_4,
  input  B_4
);

  wire nand_1_out, nand_2_out, nand_3_out, nand_4_out, not_1_out, not_2_out, or_1_out, pull_resistor_1_node,
       pull_resistor_2_node, pull_resistor_3_node, transistor_4_out;

  or or_1 (or_1_out, A, B);
  not not_1 (not_1_out, A_2);
  not not_2 (not_2_out, B_2);
  Pull_Resistor #(.pull(1)) pull_resistor_1 (.node(pull_resistor_1_node));
  Transistor #(.\type ("n")) transistor_1 (.in(1'b0), .out(pull_resistor_1_node), .gate(A_4));
  Pull_Resistor #(.pull(1)) pull_resistor_2 (.node(pull_resistor_2_node));
  Transistor #(.\type ("n")) transistor_2 (.in(1'b0), .out(pull_resistor_2_node), .gate(B_4));
  LED OUT (.in(or_1_out));
  nand nand_1 (nand_1_out, not_1_out, not_2_out);
  nand nand_2 (nand_2_out, A_3, A_3);
  nand nand_3 (nand_3_out, B_3, B_3);
  LED OUT_2 (.in(nand_1_out));
  nand nand_4 (nand_4_out, nand_2_out, nand_3_out);
  Pull_Resistor #(.pull(1)) pull_resistor_3 (.node(pull_resistor_3_node));
  Transistor #(.\type ("n")) transistor_3 (
    .in(transistor_4_out), .out(pull_resistor_3_node), .gate(pull_resistor_1_node));
  Transistor #(.\type ("n")) transistor_4 (.in(1'b0), .out(transistor_4_out), .gate(pull_resistor_2_node));
  LED OUT_3 (.in(nand_4_out));
  LED OUT_4 (.in(pull_resistor_3_node));

  // Notes on the sheet:
  //   OR
endmodule
