// Logisim project or8way.circ as structural Verilog: 1 circuit, main circuit main
module main (
  input  _1,
  input  _2,
  input  _3,
  input  _4,
  input  _5,
  input  _6,
  input  _7,
  input  _8
);

  wire or_1_out, or_2_out, or_3_out, or_4_out, or_5_out, or_6_out, or_7_out;

  or or_1 (or_1_out, _1, _2);
  or or_2 (or_2_out, or_1_out, _3);
  or or_3 (or_3_out, or_2_out, _4);
  or or_4 (or_4_out, or_3_out, _5);
  or or_5 (or_5_out, or_4_out, _6);
  or or_6 (or_6_out, or_5_out, _7);
  or or_7 (or_7_out, or_6_out, _8);
  LED OUT (.in(or_7_out));

  // Notes on the sheet:
  //   OR8WAY
endmodule
