// Logisim project xor.circ as structural Verilog: 1 circuit, main circuit main
module main (
  input  A,
  input  B,
  input  A_2,
  input  B_2,
  input  A_3,
  input  B_3
);

  wire nand_1_out, nand_2_out, nand_3_out, nand_4_out, pull_resistor_1_node, pull_resistor_2_node,
       pull_resistor_3_node, pull_resistor_4_node, transistor_2_out, transistor_4_out, transistor_6_out,
       transistor_8_out, xor_1_out;

  Pull_Resistor #(.pull(1)) pull_resistor_1 (.node(pull_resistor_1_node));
  Transistor #(.\type ("n")) transistor_1 (.in(transistor_2_out), .out(pull_resistor_1_node), .gate(A_3));
  Transistor #(.\type ("n")) transistor_2 (.in(1'b0), .out(transistor_2_out), .gate(B_3));
  xor xor_1 (xor_1_out, A, B);
  nand nand_1 (nand_1_out, A_2, B_2);
  LED OUT (.in(xor_1_out));
  nand nand_2 (nand_2_out, A_2, nand_1_out);
  nand nand_3 (nand_3_out, nand_1_out, B_2);
  Pull_Resistor #(.pull(1)) pull_resistor_2 (.node(pull_resistor_2_node));
  Transistor #(.\type ("n")) transistor_3 (.in(transistor_4_out), .out(pull_resistor_2_node), .gate(A_3));
  Transistor #(.\type ("n")) transistor_4 (.in(1'b0), .out(transistor_4_out), .gate(pull_resistor_1_node));
  Pull_Resistor #(.pull(1)) pull_resistor_3 (.node(pull_resistor_3_node));
  Transistor #(.\type ("n")) transistor_5 (
    .in(transistor_6_out), .out(pull_resistor_3_node), .gate(pull_resistor_1_node));
  Transistor #(.\type ("n")) transistor_6 (.in(1'b0), .out(transistor_6_out), .gate(B_3));
  nand nand_4 (nand_4_out, nand_2_out, nand_3_out);
  Pull_Resistor #(.pull(1)) pull_resistor_4 (.node(pull_resistor_4_node));
  Transistor #(.\type ("n")) transistor_7 (
    .in(transistor_8_out), .out(pull_resistor_4_node), .gate(pull_resistor_2_node));
  Transistor #(.\type ("n")) transistor_8 (.in(1'b0), .out(transistor_8_out), .gate(pull_resistor_3_node));
  LED OUT_2 (.in(nand_4_out));
  LED OUT_3 (.in(pull_resistor_4_node));

  // Notes on the sheet:
  //   XOR
endmodule
